# Fritzing sketch diagram_hrottle_to_pas (saved by Fritzing 0.9.10b)
circuit board: 8.46667cm x 5.64444cm
perfboards: 1

parts:
  Composant1 = Arduino Nano (Rev3.0)
  J4 = male pin header, 3 pins [form="♂ (male)"]
  J5 = male pin header, 2 pins [form="♂ (male)"]
  J6 = male alternating pin header, 3 pins [form="♂ (male)"]
  J7 = female pin header, 2 pins [form="♀ (female)"]

nets:
  GND: Composant1.GND, J4.pin2, J5.pin2, J6.pin2, J7.pin2
  N1: Composant1.D2, J4.pin1
  N2: Composant1.VIN, J5.pin1
  5V: Composant1.5V, J4.pin3, J6.pin1
  N3: Composant1.A0, J6.pin3
  N4: Composant1.D13/SCK, J7.pin1

notes:
  + Vin (7V-12V)
  Common GND
  +5V arduino
  Gnd
  Signal D2
  e-bike PAS
  +
  +5V
  S (D2)
  (with controler)
  Throttle to PAS, Chris74
  A0
  thumb throttle
  Vin 7V-12V
  Gnd commun
  S (A0)
  Controler (PAS  in)
  controler (D13)
  D13 (led builtin)
  (input_pullup)
  (not mandatory)
